// Logisim project motherboard.circ as structural Verilog: 9 circuits, main circuit main
module main (
  input  in_1,
  input  in_2,
  input  in_3,
  input  in_4,
  output out_5,
  output out_6,
  output out_7
);

  wire ALUM, and_1_out, and_2_out, and_3_out, AOUT_b0, AOUT_b1, AOUT_b2, AOUT_b3, AR, ARR, ARW, AW,
       buffer_1_out, buffer_2_out, buffer_3_out, buffer_4_out, buffer_5_out, buffer_6_out, buffer_7_out,
       buffer_8_out, buffer_9_out, buffer_10_out, buffer_11_out, buffer_12_out, buffer_13_out, buffer_14_out,
       buffer_15_out, buffer_16_out, buffer_17_out, buffer_18_out, buffer_19_out, buffer_20_out,
       buffer_21_out, buffer_22_out, buffer_23_out, buffer_24_out, buffer_25_out, buffer_26_out,
       buffer_27_out, buffer_28_out, buffer_29_out, buffer_30_out, buffer_31_out, buffer_32_out,
       buffer_33_out, buffer_34_out, buffer_35_out, buffer_36_out, buffer_37_out, buffer_38_out,
       calculationcirc_1_b1, calculationcirc_1_b2, calculationcirc_1_bl1, calculationcirc_1_bl2,
       calculationcirc_1_br1, calculationcirc_1_br2, calculationcirc_1_m1, calculationcirc_1_m2,
       calculationcirc_1_t1, calculationcirc_1_t2, calculationcirc_1_tl1, calculationcirc_1_tl2,
       calculationcirc_1_tr1, calculationcirc_1_tr2, clock_1_out, clock_2_out, D0, D1, D2, D3, DRR, DRW, DW,
       HALT, IR1R, IR2R, IR3R, IR4R, IR_b0, IR_b1, IR_b2, IR_b3, IRW, L_b0, L_b1, L_b2, L_b3, LR, LW, MAR_b0,
       MAR_b1, MAR_b2, MAR_b3, MARR, MARW, MBR_b0, MBR_b1, MBR_b2, MBR_b3, MBRR, MBRW, MyALU_a1, MyALU_a2,
       MyALU_a3, MyALU_a4, MyALU_negative, MyALU_overflow, MyALU_signed_overflow, MyALU_zero, myram_1_dr1,
       myram_1_dr2, myram_1_dr3, myram_1_dr4, or_1_out, or_2_out, or_3_out, or_4_out, or_5_out, or_6_out,
       or_7_out, or_8_out, or_9_out, or_10_out, or_11_out, or_12_out, or_13_out, or_14_out, or_15_out,
       or_16_out, or_17_out, or_18_out, or_19_out, or_20_out, or_21_out, or_22_out, or_23_out, or_24_out,
       or_25_out, or_26_out, or_27_out, or_28_out, or_29_out, or_30_out, or_31_out, PC_b0, PC_b1, PC_b2,
       PCINC, pcincr_1_out1, pcincr_1_out2, pcincr_1_out3, PCR, R0_b0, R0_b1, R0_b2, R0_b3, R0R, R0W, R1_b0,
       R1_b1, R1_b2, R1_b3, R1R, R1W, R_b0, R_b1, R_b2, R_b3, RAMM, reg4bit_1_b0, reg4bit_1_b1, reg4bit_1_b2,
       reg4bit_1_b3, RR, RW, SR, STATUS_b0, STATUS_b1, STATUS_b2, STATUS_b3, SW;

  Clock clock_1 (.out(clock_1_out));
  Clock clock_2 (.out(clock_2_out));
  or or_1 (or_1_out, myram_1_dr1, 1'b0);
  or or_2 (or_2_out, myram_1_dr2, 1'b0);
  or or_3 (or_3_out, myram_1_dr3, 1'b0);
  or or_4 (or_4_out, myram_1_dr4, 1'b0);
  and and_1 (and_1_out, ~HALT, clock_1_out);  // AND_Gate
  and and_2 (and_2_out, ~HALT, clock_2_out);  // AND_Gate
  Reg4Bit reg4bit_1 (
    .d3(D3), .d2(D2), .d1(D1), .d0(D0), .en(1'b1), .clk(and_2_out), .rw(1'b1), .b3(reg4bit_1_b3),
    .b2(reg4bit_1_b2), .b1(reg4bit_1_b1), .b0(reg4bit_1_b0));
  MyRAM myram_1 (
    .in_1(and_1_out), .DRR(DRR), .AR3(or_11_out), .AR2(or_10_out), .AR1(or_9_out), .MODE(RAMM),
    .DRI4(or_31_out), .DRI3(or_30_out), .DRI2(or_29_out), .DRI1(or_28_out), .clk(and_1_out), .ARW(ARW),
    .DRW(DRW), .DR4(myram_1_dr4), .DR3(myram_1_dr3), .DR2(myram_1_dr2), .DR1(myram_1_dr1), .Display3(D3),
    .Display2(D2), .Display1(D1), .Display0(D0));
  Reg4Bit R0 (
    .d3(or_31_out), .d2(or_30_out), .d1(or_29_out), .d0(or_28_out), .en(R0R), .clk(and_2_out), .rw(R0W),
    .b3(R0_b3), .b2(R0_b2), .b1(R0_b1), .b0(R0_b0));
  or or_5 (or_5_out, R0_b0, or_1_out);
  or or_6 (or_6_out, R0_b1, or_2_out);
  or or_7 (or_7_out, R0_b2, or_3_out);
  or or_8 (or_8_out, R0_b3, or_4_out);
  calculationcirc calculationcirc_1 (
    .D3(reg4bit_1_b3), .D2(reg4bit_1_b2), .D1(reg4bit_1_b1), .D0(reg4bit_1_b0), .B1(calculationcirc_1_b1),
    .BL1(calculationcirc_1_bl1), .BR1(calculationcirc_1_br1), .M1(calculationcirc_1_m1),
    .TL1(calculationcirc_1_tl1), .TR1(calculationcirc_1_tr1), .T1(calculationcirc_1_t1),
    .B2(calculationcirc_1_b2), .BL2(calculationcirc_1_bl2), .BR2(calculationcirc_1_br2),
    .M2(calculationcirc_1_m2), .TL2(calculationcirc_1_tl2), .TR2(calculationcirc_1_tr2),
    .T2(calculationcirc_1_t2));
  or or_9 (or_9_out, MAR_b0, or_16_out);
  or or_10 (or_10_out, MAR_b1, or_17_out);
  or or_11 (or_11_out, MAR_b2, or_18_out);
  _7_Segment_Display u_7_segment_display_1 (
    .g(calculationcirc_1_m2), .f(calculationcirc_1_tl2), .a(calculationcirc_1_t2), .b(calculationcirc_1_tr2),
    .e(calculationcirc_1_bl2), .d(calculationcirc_1_b2), .c(calculationcirc_1_br2));  // open: dp
  Reg4Bit MAR (
    .d2(or_11_out), .d1(or_10_out), .d0(or_9_out), .en(MARR), .clk(and_1_out), .rw(MARW), .b3(MAR_b3),
    .b2(MAR_b2), .b1(MAR_b1), .b0(MAR_b0));  // open: d3
  _7_Segment_Display u_7_segment_display_2 (
    .g(calculationcirc_1_m1), .f(calculationcirc_1_tl1), .a(calculationcirc_1_t1), .b(calculationcirc_1_tr1),
    .e(calculationcirc_1_bl1), .d(calculationcirc_1_b1), .c(calculationcirc_1_br1));  // open: dp
  Reg4Bit R1 (
    .d3(or_31_out), .d2(or_30_out), .d1(or_29_out), .d0(or_28_out), .en(R1R), .clk(and_2_out), .rw(R1W),
    .b3(R1_b3), .b2(R1_b2), .b1(R1_b1), .b0(R1_b0));
  or or_12 (or_12_out, R1_b0, or_5_out);
  or or_13 (or_13_out, R1_b1, or_6_out);
  or or_14 (or_14_out, R1_b2, or_7_out);
  or or_15 (or_15_out, R1_b3, or_8_out);
  buf buffer_1 (buffer_1_out, and_2_out);
  buf buffer_2 (buffer_2_out, buffer_1_out);
  buf buffer_3 (buffer_3_out, buffer_2_out);
  buf buffer_4 (buffer_4_out, buffer_3_out);
  buf buffer_5 (buffer_5_out, buffer_4_out);
  buf buffer_6 (buffer_6_out, buffer_9_out);
  buf buffer_7 (buffer_7_out, buffer_6_out);
  buf buffer_8 (buffer_8_out, buffer_5_out);
  buf buffer_9 (buffer_9_out, buffer_8_out);
  Reg4Bit MBR (
    .d3(or_31_out), .d2(or_30_out), .d1(or_29_out), .d0(or_28_out), .en(MBRR), .clk(and_1_out), .rw(MBRW),
    .b3(MBR_b3), .b2(MBR_b2), .b1(MBR_b1), .b0(MBR_b0));
  buf buffer_10 (buffer_10_out, buffer_7_out);
  buf buffer_11 (buffer_11_out, buffer_10_out);
  buf buffer_12 (buffer_12_out, buffer_11_out);
  buf buffer_13 (buffer_13_out, buffer_12_out);
  Clock clock_3 ();  // open: out
  Reg4Bit L (
    .d3(or_31_out), .d2(or_30_out), .d1(or_29_out), .d0(or_28_out), .en(LR), .clk(and_2_out), .rw(LW),
    .b3(L_b3), .b2(L_b2), .b1(L_b1), .b0(L_b0));
  buf buffer_14 (buffer_14_out, buffer_13_out);
  buf buffer_15 (buffer_15_out, buffer_14_out);
  buf buffer_16 (buffer_16_out, buffer_15_out);
  buf buffer_17 (buffer_17_out, buffer_16_out);
  or or_16 (or_16_out, PC_b0, or_23_out);
  or or_17 (or_17_out, PC_b1, 1'b0);
  or or_18 (or_18_out, PC_b2, 1'b0);
  buf buffer_18 (buffer_18_out, buffer_17_out);
  buf buffer_19 (buffer_19_out, buffer_18_out);
  buf buffer_20 (buffer_20_out, buffer_19_out);
  buf buffer_21 (buffer_21_out, buffer_20_out);
  buf buffer_22 (buffer_22_out, buffer_21_out);
  buf buffer_23 (buffer_23_out, buffer_22_out);
  buf buffer_24 (buffer_24_out, buffer_23_out);
  buf buffer_25 (buffer_25_out, buffer_24_out);
  or or_19 (or_19_out, MBR_b0, or_12_out);
  or or_20 (or_20_out, MBR_b1, or_13_out);
  or or_21 (or_21_out, MBR_b2, or_14_out);
  or or_22 (or_22_out, MBR_b3, or_15_out);
  buf buffer_26 (buffer_26_out, buffer_25_out);
  buf buffer_27 (buffer_27_out, buffer_26_out);
  buf buffer_28 (buffer_28_out, buffer_27_out);
  buf buffer_29 (buffer_29_out, buffer_28_out);
  Reg4Bit R (
    .d3(or_31_out), .d2(or_30_out), .d1(or_29_out), .d0(or_28_out), .en(RR), .clk(and_2_out), .rw(RW),
    .b3(R_b3), .b2(R_b2), .b1(R_b1), .b0(R_b0));
  buf buffer_30 (buffer_30_out, buffer_29_out);
  buf buffer_31 (buffer_31_out, buffer_30_out);
  buf buffer_32 (buffer_32_out, buffer_31_out);
  buf buffer_33 (buffer_33_out, buffer_32_out);
  Reg4Bit PC (
    .d2(pcincr_1_out1), .d1(pcincr_1_out2), .d0(pcincr_1_out3), .en(PCR), .clk(and_1_out), .rw(PCINC),
    .b2(PC_b2), .b1(PC_b1), .b0(PC_b0));  // open: d3, b3
  NewALU MyALU (
    .L4(L_b3), .L3(L_b2), .L2(L_b1), .L1(L_b0), .R4(R_b3), .R3(R_b2), .R2(R_b1), .R1(R_b0), .mode(ALUM),
    .clock(and_2_out), .signed_overflow(MyALU_signed_overflow), .negative(MyALU_negative), .zero(MyALU_zero),
    .overflow(MyALU_overflow), .A4(MyALU_a4), .A3(MyALU_a3), .A2(MyALU_a2), .A1(MyALU_a1));
  buf buffer_34 (buffer_34_out, buffer_33_out);
  buf buffer_35 (buffer_35_out, buffer_34_out);
  buf buffer_36 (buffer_36_out, buffer_35_out);
  buf buffer_37 (buffer_37_out, buffer_36_out);
  buf buffer_38 (buffer_38_out, buffer_37_out);
  or or_23 (or_23_out, and_3_out, 1'b0);
  or or_24 (or_24_out, AOUT_b0, or_19_out);
  or or_25 (or_25_out, AOUT_b1, or_20_out);
  or or_26 (or_26_out, AOUT_b2, or_21_out);
  or or_27 (or_27_out, AOUT_b3, or_22_out);
  Reg4Bit IR (
    .d3(or_31_out), .d2(or_30_out), .d1(or_29_out), .d0(or_28_out), .en(1'b1), .clk(and_1_out), .rw(IRW),
    .b3(IR_b3), .b2(IR_b2), .b1(IR_b1), .b0(IR_b0));
  and and_3 (and_3_out, IR4R, IR_b0);
  Reg4Bit STATUS (
    .d3(MyALU_overflow), .d2(MyALU_signed_overflow), .d1(MyALU_zero), .d0(MyALU_negative), .en(SR),
    .clk(and_2_out), .rw(SW), .b3(STATUS_b3), .b2(STATUS_b2), .b1(STATUS_b1), .b0(STATUS_b0));
  or or_28 (or_28_out, STATUS_b0, or_24_out);
  or or_29 (or_29_out, STATUS_b1, or_25_out);
  or or_30 (or_30_out, STATUS_b2, or_26_out);
  or or_31 (or_31_out, STATUS_b3, or_27_out);
  pcincr pcincr_1 (
    .in1(PC_b2), .in2(PC_b1), .in3(PC_b0), .en(PCINC), .out1(pcincr_1_out1), .out2(pcincr_1_out2),
    .out3(pcincr_1_out3));
  Reg4Bit AOUT (
    .d3(MyALU_a4), .d2(MyALU_a3), .d1(MyALU_a2), .d0(MyALU_a1), .en(AR), .clk(buffer_38_out), .rw(AW),
    .b3(AOUT_b3), .b2(AOUT_b2), .b1(AOUT_b1), .b0(AOUT_b0));
  pcincr pcincr_2 (.in1(in_1), .in2(in_2), .in3(in_3), .en(in_4), .out1(out_5), .out2(out_6), .out3(out_7));
  CU ControlUnit (
    .i1(IR_b3), .i2(IR_b2), .in_3(IR_b1), .i4(IR_b0), .IR1read(IR1R), .IR2read(IR2R), .IR3read(IR3R),
    .IR4read(IR4R), .MARwrite(MARW), .MARread(MARR), .MBRwrite(MBRW), .MBRread(MBRR), .ARwrite(ARW),
    .ARread(ARR), .DRwrite(DRW), .DRread(DRR), .RAMmode(RAMM), .PCincr(PCINC), .PCread(PCR), .IRwrite(IRW),
    .IRread(DW), .out_22(R0W), .out_23(R0R), .out_24(R1W), .out_25(R1R), .Lwrite(LW), .Lread(LR),
    .Rwrite(RW), .Rread(RR), .Awrite(AW), .Aread(AR), .STATUSwrite(SW), .STATUSread(SR), .ALUmode(ALUM),
    .CLOCKwrite(HALT));

  // Notes on the sheet:
  //   ADR IS ONLY 1 OR 0
  //   Mode 0 = W  1 = R
  //   D1
  //   D2
  //   D3
  //   D4
  //   D1
  //   D4
  //   A1
  //   A2
  //   A3
  //   3 bit address
  //   A1
  //   PC | INCrementor
  //   MBR Write
endmodule

module MyRAM (
  input  in_1,
  input  DRR,
  input  AR3,
  input  AR2,
  input  AR1,
  input  MODE,
  input  DRI4,
  input  DRI3,
  input  DRI2,
  input  DRI1,
  input  clk,
  input  ARW,
  input  DRW,
  output DR4,
  output DR3,
  output DR2,
  output DR1,
  output Display3,
  output Display2,
  output Display1,
  output Display0
);

  wire and_1_out, and_2_out, and_3_out, and_4_out, and_5_out, and_6_out, and_7_out, and_8_out, and_9_out,
       and_10_out, and_11_out, and_12_out, and_13_out, and_14_out, and_15_out, and_16_out, and_17_out,
       and_18_out, and_19_out, and_20_out, and_21_out, and_22_out, and_23_out, and_24_out, and_25_out,
       and_26_out, and_27_out, and_28_out, and_29_out, and_30_out, and_31_out, and_32_out, and_33_out,
       and_34_out, and_35_out, and_36_out, and_37_out, and_38_out, and_39_out, and_40_out, and_41_out,
       and_42_out, and_43_out, and_44_out, and_45_out, and_46_out, and_47_out, and_48_out, and_49_out,
       and_50_out, and_51_out, and_52_out, and_53_out, and_54_out, and_55_out, and_56_out, and_57_out,
       and_58_out, and_59_out, and_60_out, and_61_out, and_62_out, and_63_out, and_64_out, and_65_out,
       and_66_out, and_67_out, and_68_out, and_69_out, and_70_out, and_71_out, and_72_out, and_75_out,
       and_76_out, and_77_out, and_78_out, and_79_out, and_80_out, and_81_out, and_82_out, and_84_out,
       and_85_out, and_86_out, and_87_out, and_88_out, and_89_out, and_90_out, and_91_out, buffer_1_out,
       buffer_2_out, buffer_3_out, buffer_4_out, buffer_5_out, buffer_6_out, buffer_7_out, buffer_8_out,
       buffer_9_out, buffer_10_out, buffer_11_out, buffer_12_out, buffer_13_out, buffer_14_out,
       buffer_15_out, buffer_16_out, buffer_17_out, buffer_18_out, buffer_19_out, buffer_20_out,
       buffer_21_out, buffer_22_out, buffer_23_out, buffer_24_out, buffer_25_out, buffer_26_out,
       buffer_27_out, buffer_28_out, buffer_29_out, buffer_30_out, buffer_31_out, buffer_32_out,
       buffer_33_out, buffer_34_out, buffer_35_out, buffer_37_out, buffer_38_out, buffer_39_out,
       buffer_40_out, buffer_41_out, buffer_42_out, buffer_43_out, buffer_44_out, buffer_45_out,
       buffer_46_out, buffer_47_out, buffer_48_out, buffer_49_out, buffer_50_out, buffer_51_out,
       buffer_52_out, buffer_53_out, buffer_54_out, buffer_55_out, buffer_56_out, buffer_57_out,
       buffer_58_out, buffer_59_out, buffer_60_out, buffer_61_out, buffer_62_out, buffer_63_out,
       buffer_64_out, buffer_65_out, buffer_66_out, buffer_67_out, buffer_68_out, buffer_69_out,
       buffer_70_out, buffer_71_out, buffer_72_out, buffer_73_out, buffer_74_out, buffer_75_out,
       buffer_76_out, buffer_77_out, buffer_78_out, buffer_79_out, buffer_80_out, buffer_81_out,
       buffer_82_out, buffer_83_out, buffer_84_out, buffer_85_out, buffer_86_out, buffer_87_out,
       buffer_88_out, buffer_89_out, buffer_90_out, buffer_91_out, buffer_92_out, buffer_93_out,
       buffer_94_out, buffer_95_out, buffer_96_out, buffer_97_out, buffer_98_out, buffer_99_out,
       buffer_100_out, buffer_101_out, buffer_102_out, buffer_103_out, buffer_104_out, buffer_105_out,
       buffer_106_out, buffer_107_out, buffer_108_out, buffer_109_out, buffer_110_out, buffer_111_out,
       buffer_112_out, buffer_113_out, buffer_114_out, buffer_115_out, buffer_116_out, buffer_117_out,
       buffer_118_out, buffer_119_out, buffer_120_out, buffer_121_out, buffer_122_out, buffer_123_out,
       buffer_124_out, buffer_125_out, buffer_126_out, buffer_127_out, buffer_128_out, buffer_129_out,
       buffer_130_out, buffer_131_out, buffer_132_out, buffer_133_out, buffer_134_out, buffer_135_out,
       buffer_136_out, buffer_137_out, buffer_138_out, buffer_139_out, buffer_140_out, buffer_141_out,
       buffer_142_out, buffer_143_out, buffer_144_out, buffer_145_out, buffer_146_out, buffer_147_out,
       buffer_148_out, buffer_149_out, buffer_150_out, buffer_151_out, buffer_152_out, buffer_153_out,
       buffer_154_out, buffer_155_out, buffer_156_out, buffer_157_out, buffer_158_out, buffer_159_out,
       buffer_160_out, buffer_161_out, buffer_162_out, buffer_163_out, buffer_164_out, buffer_165_out,
       buffer_166_out, buffer_167_out, buffer_168_out, buffer_169_out, buffer_170_out, buffer_171_out,
       buffer_172_out, buffer_173_out, buffer_174_out, buffer_175_out, buffer_176_out, buffer_177_out,
       buffer_178_out, buffer_179_out, buffer_180_out, buffer_181_out, buffer_182_out, buffer_183_out,
       buffer_184_out, buffer_185_out, buffer_186_out, buffer_187_out, buffer_188_out, buffer_189_out,
       buffer_190_out, buffer_191_out, buffer_192_out, buffer_193_out, buffer_194_out, buffer_195_out,
       buffer_196_out, buffer_197_out, buffer_198_out, buffer_199_out, buffer_200_out, buffer_201_out,
       buffer_202_out, buffer_203_out, buffer_204_out, buffer_205_out, buffer_206_out, buffer_207_out,
       buffer_208_out, buffer_209_out, buffer_210_out, buffer_211_out, buffer_212_out, buffer_213_out,
       buffer_214_out, buffer_215_out, d_ff_1_q, d_ff_2_q, d_ff_3_q, d_ff_4_q, d_ff_5_q, d_ff_6_q, d_ff_7_q,
       d_ff_8_q, d_ff_9_q, d_ff_10_q, d_ff_11_q, d_ff_13_q, d_ff_14_q, d_ff_15_q, d_ff_16_q, d_ff_17_q,
       d_ff_18_q, d_ff_19_q, d_ff_20_q, d_ff_21_q, d_ff_23_q, d_ff_24_q, d_ff_25_q, d_ff_26_q, d_ff_27_q,
       d_ff_28_q, d_ff_29_q, d_ff_30_q, d_ff_31_q, d_ff_32_q, d_ff_33_q, d_ff_34_q, d_ff_35_q, d_ff_37_q,
       d_ff_38_q, d_ff_39_q, d_ff_40_q, d_ff_41_q, d_ff_42_q, d_ff_43_q, not_1_out, not_2_out, not_3_out,
       not_4_out, not_5_out, not_6_out, not_7_out, not_8_out, not_9_out, not_10_out, not_11_out, or_1_out,
       or_2_out, or_3_out, or_4_out;

  D_Flip_Flop #(.trigger("falling")) d_ff_1 (.D(AR3), .clk(and_1_out), .Q(d_ff_1_q));  // open: Qn, preset, reset
  and and_1 (and_1_out, buffer_208_out, ARW);
  buf buffer_1 (buffer_1_out, in_1);
  buf buffer_2 (buffer_2_out, buffer_1_out);
  buf buffer_3 (buffer_3_out, buffer_2_out);
  buf buffer_4 (buffer_4_out, buffer_3_out);
  buf buffer_5 (buffer_5_out, buffer_4_out);
  buf buffer_6 (buffer_6_out, buffer_5_out);
  buf buffer_7 (buffer_7_out, buffer_6_out);
  buf buffer_8 (buffer_8_out, buffer_7_out);
  buf buffer_9 (buffer_9_out, buffer_8_out);
  buf buffer_10 (buffer_10_out, buffer_9_out);
  buf buffer_11 (buffer_11_out, buffer_10_out);
  buf buffer_12 (buffer_12_out, buffer_13_out);
  buf buffer_13 (buffer_13_out, buffer_14_out);
  buf buffer_14 (buffer_14_out, buffer_15_out);
  buf buffer_15 (buffer_15_out, buffer_16_out);
  buf buffer_16 (buffer_16_out, buffer_17_out);
  buf buffer_17 (buffer_17_out, buffer_18_out);
  buf buffer_18 (buffer_18_out, buffer_11_out);
  buf buffer_19 (buffer_19_out, buffer_11_out);
  // Buffer buffer_20 has open pins: in=open, out=buffer_20_out
  buf buffer_21 (buffer_21_out, buffer_19_out);
  buf buffer_22 (buffer_22_out, buffer_20_out);
  buf buffer_23 (buffer_23_out, buffer_21_out);
  buf buffer_24 (buffer_24_out, buffer_22_out);
  buf buffer_25 (buffer_25_out, buffer_23_out);
  buf buffer_26 (buffer_26_out, buffer_24_out);
  buf buffer_27 (buffer_27_out, buffer_25_out);
  buf buffer_28 (buffer_28_out, buffer_26_out);
  buf buffer_29 (buffer_29_out, buffer_27_out);
  buf buffer_30 (buffer_30_out, buffer_28_out);
  buf buffer_31 (buffer_31_out, buffer_29_out);
  buf buffer_32 (buffer_32_out, buffer_30_out);
  buf buffer_33 (buffer_33_out, buffer_31_out);
  buf buffer_34 (buffer_34_out, buffer_32_out);
  buf buffer_35 (buffer_35_out, buffer_33_out);
  // Buffer buffer_36 has open pins: in=buffer_34_out, out=open
  buf buffer_37 (buffer_37_out, buffer_35_out);
  D_Flip_Flop #(.trigger("falling")) d_ff_2 (.D(AR2), .clk(and_2_out), .Q(d_ff_2_q));  // open: Qn, preset, reset
  and and_2 (and_2_out, buffer_208_out, ARW);
  buf buffer_38 (buffer_38_out, buffer_39_out);
  buf buffer_39 (buffer_39_out, buffer_40_out);
  buf buffer_40 (buffer_40_out, buffer_41_out);
  buf buffer_41 (buffer_41_out, buffer_42_out);
  buf buffer_42 (buffer_42_out, buffer_43_out);
  buf buffer_43 (buffer_43_out, buffer_44_out);
  buf buffer_44 (buffer_44_out, buffer_45_out);
  buf buffer_45 (buffer_45_out, buffer_46_out);
  buf buffer_46 (buffer_46_out, buffer_47_out);
  buf buffer_47 (buffer_47_out, buffer_48_out);
  buf buffer_48 (buffer_48_out, buffer_49_out);
  buf buffer_49 (buffer_49_out, buffer_50_out);
  buf buffer_50 (buffer_50_out, buffer_51_out);
  buf buffer_51 (buffer_51_out, buffer_52_out);
  buf buffer_52 (buffer_52_out, buffer_53_out);
  buf buffer_53 (buffer_53_out, buffer_54_out);
  buf buffer_54 (buffer_54_out, buffer_55_out);
  buf buffer_55 (buffer_55_out, buffer_57_out);
  buf buffer_56 (buffer_56_out, buffer_12_out);
  buf buffer_57 (buffer_57_out, buffer_56_out);
  buf buffer_58 (buffer_58_out, d_ff_2_q);
  buf buffer_59 (buffer_59_out, d_ff_3_q);
  buf buffer_60 (buffer_60_out, d_ff_1_q);
  buf buffer_61 (buffer_61_out, d_ff_2_q);
  not not_1 (not_1_out, d_ff_3_q);
  buf buffer_62 (buffer_62_out, d_ff_1_q);
  not not_2 (not_2_out, d_ff_2_q);
  buf buffer_63 (buffer_63_out, d_ff_3_q);
  buf buffer_64 (buffer_64_out, d_ff_1_q);
  not not_3 (not_3_out, d_ff_2_q);
  buf buffer_65 (buffer_65_out, d_ff_3_q);
  not not_4 (not_4_out, d_ff_1_q);
  buf buffer_66 (buffer_66_out, d_ff_2_q);
  buf buffer_67 (buffer_67_out, d_ff_3_q);
  not not_5 (not_5_out, d_ff_1_q);
  buf buffer_68 (buffer_68_out, d_ff_2_q);
  buf buffer_69 (buffer_69_out, d_ff_3_q);
  not not_6 (not_6_out, d_ff_1_q);
  not not_7 (not_7_out, d_ff_2_q);
  buf buffer_70 (buffer_70_out, buffer_11_out);
  buf buffer_71 (buffer_71_out, d_ff_3_q);
  Clock clock_1 ();  // open: out
  not not_8 (not_8_out, d_ff_1_q);
  not not_9 (not_9_out, d_ff_2_q);
  not not_10 (not_10_out, d_ff_3_q);
  buf buffer_72 (buffer_72_out, buffer_37_out);
  buf buffer_73 (buffer_73_out, buffer_72_out);
  buf buffer_74 (buffer_74_out, buffer_73_out);
  buf buffer_75 (buffer_75_out, buffer_74_out);
  D_Flip_Flop #(.trigger("falling")) d_ff_3 (.D(AR1), .clk(and_3_out), .Q(d_ff_3_q));  // open: Qn, preset, reset
  and and_3 (and_3_out, buffer_208_out, ARW);
  buf buffer_76 (buffer_76_out, buffer_38_out);
  buf buffer_77 (buffer_77_out, buffer_76_out);
  buf buffer_78 (buffer_78_out, buffer_77_out);
  buf buffer_79 (buffer_79_out, buffer_78_out);
  and and_4 (and_4_out, d_ff_1_q, buffer_58_out, buffer_11_out, buffer_59_out);
  and and_5 (and_5_out, and_4_out, DRW, not_11_out);
  and and_6 (and_6_out, buffer_60_out, buffer_61_out, buffer_11_out, not_1_out);
  and and_7 (and_7_out, and_6_out, DRW, not_11_out);
  and and_8 (and_8_out, buffer_62_out, not_2_out, buffer_11_out, buffer_63_out);
  and and_9 (and_9_out, and_8_out, DRW, not_11_out);
  and and_10 (and_10_out, buffer_64_out, not_3_out, buffer_11_out, buffer_65_out);
  and and_11 (and_11_out, and_10_out, DRW, not_11_out);
  and and_12 (and_12_out, not_4_out, buffer_66_out, buffer_11_out, buffer_67_out);
  and and_13 (and_13_out, and_12_out, DRW, not_11_out);
  and and_14 (and_14_out, not_5_out, buffer_68_out, buffer_11_out, buffer_69_out);
  and and_15 (and_15_out, and_14_out, DRW, not_11_out);
  and and_16 (and_16_out, not_6_out, not_7_out, buffer_70_out, buffer_71_out);
  and and_17 (and_17_out, and_16_out, DRW, not_11_out);
  and and_18 (and_18_out, not_8_out, not_9_out, buffer_11_out, not_10_out);
  and and_19 (and_19_out, and_18_out, DRW, not_11_out);
  buf buffer_80 (buffer_80_out, buffer_75_out);
  buf buffer_81 (buffer_81_out, buffer_80_out);
  D_Flip_Flop d_ff_4 (.D(MODE), .clk(buffer_81_out), .Q(d_ff_4_q));  // open: Qn, preset, reset
  buf buffer_82 (buffer_82_out, buffer_79_out);
  buf buffer_83 (buffer_83_out, buffer_82_out);
  buf buffer_84 (buffer_84_out, buffer_83_out);
  buf buffer_85 (buffer_85_out, buffer_84_out);
  not not_11 (not_11_out, d_ff_4_q);
  buf buffer_86 (buffer_86_out, buffer_85_out);
  buf buffer_87 (buffer_87_out, buffer_86_out);
  buf buffer_88 (buffer_88_out, buffer_87_out);
  buf buffer_89 (buffer_89_out, buffer_88_out);
  and and_20 (and_20_out, and_4_out, not_11_out, d_ff_13_q);
  D_Flip_Flop #(.trigger("high")) d_ff_5 (.D(and_20_out), .clk(and_5_out), .Q(d_ff_5_q));  // open: Qn, preset, reset
  and and_21 (and_21_out, and_6_out, not_11_out, d_ff_13_q);
  D_Flip_Flop #(.trigger("high")) d_ff_6 (.D(and_21_out), .clk(and_7_out), .Q(d_ff_6_q));  // open: Qn, preset, reset
  and and_22 (and_22_out, and_8_out, not_11_out, d_ff_13_q);
  D_Flip_Flop #(.trigger("high")) d_ff_7 (.D(and_22_out), .clk(and_9_out), .Q(d_ff_7_q));  // open: Qn, preset, reset
  and and_23 (and_23_out, and_10_out, not_11_out, d_ff_13_q);
  D_Flip_Flop #(.trigger("high")) d_ff_8 (.D(and_23_out), .clk(and_11_out), .Q(d_ff_8_q));  // open: Qn, preset, reset
  and and_24 (and_24_out, and_12_out, not_11_out, d_ff_13_q);
  D_Flip_Flop #(.trigger("high")) d_ff_9 (.D(and_24_out), .clk(and_13_out), .Q(d_ff_9_q));  // open: Qn, preset, reset
  and and_25 (and_25_out, and_14_out, not_11_out, d_ff_13_q);
  D_Flip_Flop #(.trigger("high")) d_ff_10 (.D(and_25_out), .clk(and_15_out), .Q(d_ff_10_q));  // open: Qn, preset, reset
  and and_26 (and_26_out, and_16_out, not_11_out, d_ff_13_q);
  D_Flip_Flop #(.trigger("high")) d_ff_11 (.D(and_26_out), .clk(and_17_out), .Q(d_ff_11_q));  // open: Qn, preset, reset
  and and_27 (and_27_out, and_18_out, not_11_out, d_ff_13_q);
  D_Flip_Flop #(.trigger("high")) d_ff_12 (.D(and_27_out), .clk(and_19_out), .Q(Display3));  // open: Qn, preset, reset
  buf buffer_90 (buffer_90_out, clk);
  buf buffer_91 (buffer_91_out, buffer_90_out);
  buf buffer_92 (buffer_92_out, buffer_91_out);
  buf buffer_93 (buffer_93_out, buffer_92_out);
  buf buffer_94 (buffer_94_out, buffer_93_out);
  buf buffer_95 (buffer_95_out, buffer_94_out);
  buf buffer_96 (buffer_96_out, buffer_95_out);
  buf buffer_97 (buffer_97_out, buffer_96_out);
  buf buffer_98 (buffer_98_out, buffer_97_out);
  buf buffer_99 (buffer_99_out, buffer_89_out);
  buf buffer_100 (buffer_100_out, buffer_99_out);
  buf buffer_101 (buffer_101_out, buffer_100_out);
  buf buffer_102 (buffer_102_out, buffer_101_out);
  or or_1 (or_1_out, and_28_out, and_29_out, and_30_out, and_31_out, and_32_out, and_33_out, and_34_out, and_35_out);
  and and_28 (and_28_out, d_ff_5_q, and_4_out, d_ff_4_q);
  and and_29 (and_29_out, d_ff_6_q, and_6_out, d_ff_4_q);
  and and_30 (and_30_out, d_ff_7_q, and_8_out, d_ff_4_q);
  and and_31 (and_31_out, d_ff_8_q, and_10_out, d_ff_4_q);
  and and_32 (and_32_out, d_ff_9_q, and_12_out, d_ff_4_q);
  and and_33 (and_33_out, d_ff_10_q, and_14_out, d_ff_4_q);
  and and_34 (and_34_out, d_ff_11_q, and_16_out, d_ff_4_q);
  and and_35 (and_35_out, Display3, and_18_out, d_ff_4_q);
  D_Flip_Flop #(.trigger("falling")) d_ff_13 (.D(DRI4), .clk(and_36_out), .Q(d_ff_13_q));  // open: Qn, preset, reset
  and and_36 (and_36_out, buffer_208_out, DRW);
  buf buffer_103 (buffer_103_out, buffer_104_out);
  buf buffer_104 (buffer_104_out, buffer_113_out);
  buf buffer_105 (buffer_105_out, buffer_102_out);
  buf buffer_106 (buffer_106_out, buffer_105_out);
  buf buffer_107 (buffer_107_out, buffer_106_out);
  buf buffer_108 (buffer_108_out, buffer_107_out);
  D_Flip_Flop #(.trigger("falling")) d_ff_14 (.D(DRI3), .clk(and_37_out), .Q(d_ff_14_q));  // open: Qn, preset, reset
  and and_37 (and_37_out, buffer_208_out, DRW);
  buf buffer_109 (buffer_109_out, buffer_103_out);
  buf buffer_110 (buffer_110_out, buffer_109_out);
  buf buffer_111 (buffer_111_out, buffer_110_out);
  buf buffer_112 (buffer_112_out, buffer_111_out);
  buf buffer_113 (buffer_113_out, buffer_114_out);
  buf buffer_114 (buffer_114_out, buffer_115_out);
  buf buffer_115 (buffer_115_out, buffer_116_out);
  buf buffer_116 (buffer_116_out, buffer_126_out);
  buf buffer_117 (buffer_117_out, buffer_98_out);
  buf buffer_118 (buffer_118_out, buffer_117_out);
  buf buffer_119 (buffer_119_out, buffer_118_out);
  buf buffer_120 (buffer_120_out, buffer_119_out);
  buf buffer_121 (buffer_121_out, buffer_108_out);
  and and_38 (and_38_out, buffer_121_out, DRR);
  and and_39 (and_39_out, and_4_out, not_11_out, d_ff_14_q);
  D_Flip_Flop #(.trigger("high")) d_ff_15 (.D(and_39_out), .clk(and_5_out), .Q(d_ff_15_q));  // open: Qn, preset, reset
  and and_40 (and_40_out, and_6_out, not_11_out, d_ff_14_q);
  D_Flip_Flop #(.trigger("high")) d_ff_16 (.D(and_40_out), .clk(and_7_out), .Q(d_ff_16_q));  // open: Qn, preset, reset
  and and_41 (and_41_out, and_8_out, not_11_out, d_ff_14_q);
  D_Flip_Flop #(.trigger("high")) d_ff_17 (.D(and_41_out), .clk(and_9_out), .Q(d_ff_17_q));  // open: Qn, preset, reset
  and and_42 (and_42_out, and_10_out, not_11_out, d_ff_14_q);
  D_Flip_Flop #(.trigger("high")) d_ff_18 (.D(and_42_out), .clk(and_11_out), .Q(d_ff_18_q));  // open: Qn, preset, reset
  and and_43 (and_43_out, and_12_out, not_11_out, d_ff_14_q);
  D_Flip_Flop #(.trigger("high")) d_ff_19 (.D(and_43_out), .clk(and_13_out), .Q(d_ff_19_q));  // open: Qn, preset, reset
  and and_44 (and_44_out, and_14_out, not_11_out, d_ff_14_q);
  D_Flip_Flop #(.trigger("high")) d_ff_20 (.D(and_44_out), .clk(and_15_out), .Q(d_ff_20_q));  // open: Qn, preset, reset
  and and_45 (and_45_out, and_16_out, not_11_out, d_ff_14_q);
  D_Flip_Flop #(.trigger("high")) d_ff_21 (.D(and_45_out), .clk(and_17_out), .Q(d_ff_21_q));  // open: Qn, preset, reset
  and and_46 (and_46_out, and_18_out, not_11_out, d_ff_14_q);
  D_Flip_Flop #(.trigger("high")) d_ff_22 (.D(and_46_out), .clk(and_19_out), .Q(Display2));  // open: Qn, preset, reset
  D_Flip_Flop #(.trigger("falling")) d_ff_23 (.D(DRI2), .clk(and_47_out), .Q(d_ff_23_q));  // open: Qn, preset, reset
  and and_47 (and_47_out, buffer_208_out, DRW);
  buf buffer_122 (buffer_122_out, buffer_112_out);
  buf buffer_123 (buffer_123_out, buffer_122_out);
  buf buffer_124 (buffer_124_out, buffer_123_out);
  buf buffer_125 (buffer_125_out, buffer_124_out);
  buf buffer_126 (buffer_126_out, buffer_127_out);
  buf buffer_127 (buffer_127_out, buffer_128_out);
  buf buffer_128 (buffer_128_out, buffer_129_out);
  buf buffer_129 (buffer_129_out, buffer_138_out);
  buf buffer_130 (buffer_130_out, buffer_120_out);
  buf buffer_131 (buffer_131_out, buffer_130_out);
  buf buffer_132 (buffer_132_out, buffer_131_out);
  buf buffer_133 (buffer_133_out, buffer_132_out);
  D_Flip_Flop d_ff_24 (.D(or_1_out), .clk(and_38_out), .Q(d_ff_24_q));  // open: Qn, preset, reset
  or or_2 (or_2_out, and_48_out, and_49_out, and_50_out, and_51_out, and_52_out, and_53_out, and_54_out, and_55_out);
  and and_48 (and_48_out, d_ff_15_q, and_4_out, d_ff_4_q);
  and and_49 (and_49_out, d_ff_16_q, and_6_out, d_ff_4_q);
  and and_50 (and_50_out, d_ff_17_q, and_8_out, d_ff_4_q);
  and and_51 (and_51_out, d_ff_18_q, and_10_out, d_ff_4_q);
  and and_52 (and_52_out, d_ff_19_q, and_12_out, d_ff_4_q);
  and and_53 (and_53_out, d_ff_20_q, and_14_out, d_ff_4_q);
  and and_54 (and_54_out, d_ff_21_q, and_16_out, d_ff_4_q);
  and and_55 (and_55_out, Display2, and_18_out, d_ff_4_q);
  D_Flip_Flop #(.trigger("falling")) d_ff_25 (.D(DRI1), .clk(and_56_out), .Q(d_ff_25_q));  // open: Qn, preset, reset
  and and_56 (and_56_out, buffer_208_out, DRW);
  buf buffer_134 (buffer_134_out, buffer_125_out);
  buf buffer_135 (buffer_135_out, buffer_134_out);
  buf buffer_136 (buffer_136_out, buffer_135_out);
  buf buffer_137 (buffer_137_out, buffer_136_out);
  buf buffer_138 (buffer_138_out, buffer_139_out);
  buf buffer_139 (buffer_139_out, buffer_140_out);
  buf buffer_140 (buffer_140_out, buffer_141_out);
  buf buffer_141 (buffer_141_out, buffer_150_out);
  buf buffer_142 (buffer_142_out, buffer_133_out);
  buf buffer_143 (buffer_143_out, buffer_142_out);
  buf buffer_144 (buffer_144_out, buffer_143_out);
  buf buffer_145 (buffer_145_out, buffer_144_out);
  D_Flip_Flop d_ff_26 (.D(or_2_out), .clk(and_38_out), .Q(d_ff_26_q));  // open: Qn, preset, reset
  buf buffer_146 (buffer_146_out, buffer_137_out);
  buf buffer_147 (buffer_147_out, buffer_146_out);
  buf buffer_148 (buffer_148_out, buffer_147_out);
  buf buffer_149 (buffer_149_out, buffer_148_out);
  buf buffer_150 (buffer_150_out, buffer_151_out);
  buf buffer_151 (buffer_151_out, buffer_152_out);
  buf buffer_152 (buffer_152_out, buffer_153_out);
  buf buffer_153 (buffer_153_out, buffer_162_out);
  buf buffer_154 (buffer_154_out, buffer_145_out);
  buf buffer_155 (buffer_155_out, buffer_154_out);
  buf buffer_156 (buffer_156_out, buffer_155_out);
  buf buffer_157 (buffer_157_out, buffer_156_out);
  D_Flip_Flop d_ff_27 (.D(or_3_out), .clk(and_38_out), .Q(d_ff_27_q));  // open: Qn, preset, reset
  and and_57 (and_57_out, and_4_out, not_11_out, d_ff_23_q);
  and and_58 (and_58_out, and_6_out, not_11_out, d_ff_23_q);
  and and_59 (and_59_out, and_8_out, not_11_out, d_ff_23_q);
  and and_60 (and_60_out, and_10_out, not_11_out, d_ff_23_q);
  and and_61 (and_61_out, and_12_out, not_11_out, d_ff_23_q);
  and and_62 (and_62_out, and_14_out, not_11_out, d_ff_23_q);
  and and_63 (and_63_out, and_16_out, not_11_out, d_ff_23_q);
  and and_64 (and_64_out, and_18_out, not_11_out, d_ff_23_q);
  buf buffer_158 (buffer_158_out, buffer_149_out);
  buf buffer_159 (buffer_159_out, buffer_158_out);
  buf buffer_160 (buffer_160_out, buffer_159_out);
  buf buffer_161 (buffer_161_out, buffer_160_out);
  buf buffer_162 (buffer_162_out, buffer_163_out);
  buf buffer_163 (buffer_163_out, buffer_164_out);
  buf buffer_164 (buffer_164_out, buffer_165_out);
  buf buffer_165 (buffer_165_out, buffer_176_out);
  buf buffer_166 (buffer_166_out, buffer_157_out);
  buf buffer_167 (buffer_167_out, buffer_166_out);
  buf buffer_168 (buffer_168_out, buffer_167_out);
  buf buffer_169 (buffer_169_out, buffer_168_out);
  D_Flip_Flop d_ff_28 (.D(or_4_out), .clk(and_38_out), .Q(d_ff_28_q));  // open: Qn, preset, reset
  D_Flip_Flop #(.trigger("high")) d_ff_29 (.D(and_57_out), .clk(and_5_out), .Q(d_ff_29_q));  // open: Qn, preset, reset
  D_Flip_Flop #(.trigger("high")) d_ff_30 (.D(and_58_out), .clk(and_7_out), .Q(d_ff_30_q));  // open: Qn, preset, reset
  D_Flip_Flop #(.trigger("high")) d_ff_31 (.D(and_59_out), .clk(and_9_out), .Q(d_ff_31_q));  // open: Qn, preset, reset
  D_Flip_Flop #(.trigger("high")) d_ff_32 (.D(and_60_out), .clk(and_11_out), .Q(d_ff_32_q));  // open: Qn, preset, reset
  D_Flip_Flop #(.trigger("high")) d_ff_33 (.D(and_61_out), .clk(and_13_out), .Q(d_ff_33_q));  // open: Qn, preset, reset
  D_Flip_Flop #(.trigger("high")) d_ff_34 (.D(and_62_out), .clk(and_15_out), .Q(d_ff_34_q));  // open: Qn, preset, reset
  D_Flip_Flop #(.trigger("high")) d_ff_35 (.D(and_63_out), .clk(and_17_out), .Q(d_ff_35_q));  // open: Qn, preset, reset
  D_Flip_Flop #(.trigger("high")) d_ff_36 (.D(and_64_out), .clk(and_19_out), .Q(Display1));  // open: Qn, preset, reset
  Clock clock_2 ();  // open: out
  buf buffer_170 (buffer_170_out, buffer_173_out);
  buf buffer_171 (buffer_171_out, buffer_170_out);
  buf buffer_172 (buffer_172_out, buffer_161_out);
  buf buffer_173 (buffer_173_out, buffer_172_out);
  buf buffer_174 (buffer_174_out, buffer_175_out);
  buf buffer_175 (buffer_175_out, buffer_186_out);
  buf buffer_176 (buffer_176_out, buffer_177_out);
  buf buffer_177 (buffer_177_out, buffer_174_out);
  buf buffer_178 (buffer_178_out, buffer_181_out);
  buf buffer_179 (buffer_179_out, buffer_178_out);
  buf buffer_180 (buffer_180_out, buffer_169_out);
  buf buffer_181 (buffer_181_out, buffer_180_out);
  or or_3 (or_3_out, and_65_out, and_66_out, and_67_out, and_68_out, and_69_out, and_70_out, and_71_out, and_72_out);
  and and_65 (and_65_out, d_ff_29_q, and_4_out, d_ff_4_q);
  and and_66 (and_66_out, d_ff_30_q, and_6_out, d_ff_4_q);
  and and_67 (and_67_out, d_ff_31_q, and_8_out, d_ff_4_q);
  and and_68 (and_68_out, d_ff_32_q, and_10_out, d_ff_4_q);
  and and_69 (and_69_out, d_ff_33_q, and_12_out, d_ff_4_q);
  and and_70 (and_70_out, d_ff_34_q, and_14_out, d_ff_4_q);
  and and_71 (and_71_out, d_ff_35_q, and_16_out, d_ff_4_q);
  and and_72 (and_72_out, Display1, and_18_out, d_ff_4_q);
  buf buffer_182 (buffer_182_out, buffer_171_out);
  buf buffer_183 (buffer_183_out, buffer_182_out);
  buf buffer_184 (buffer_184_out, buffer_183_out);
  buf buffer_185 (buffer_185_out, buffer_184_out);
  buf buffer_186 (buffer_186_out, buffer_187_out);
  buf buffer_187 (buffer_187_out, buffer_188_out);
  buf buffer_188 (buffer_188_out, buffer_189_out);
  buf buffer_189 (buffer_189_out, buffer_198_out);
  buf buffer_190 (buffer_190_out, buffer_179_out);
  buf buffer_191 (buffer_191_out, buffer_190_out);
  buf buffer_192 (buffer_192_out, buffer_191_out);
  buf buffer_193 (buffer_193_out, buffer_192_out);
  and and_73 (DR4, DRR, d_ff_24_q);
  buf buffer_194 (buffer_194_out, buffer_185_out);
  buf buffer_195 (buffer_195_out, buffer_194_out);
  buf buffer_196 (buffer_196_out, buffer_195_out);
  buf buffer_197 (buffer_197_out, buffer_196_out);
  buf buffer_198 (buffer_198_out, buffer_199_out);
  buf buffer_199 (buffer_199_out, buffer_200_out);
  buf buffer_200 (buffer_200_out, buffer_201_out);
  buf buffer_201 (buffer_201_out, buffer_209_out);
  buf buffer_202 (buffer_202_out, buffer_193_out);
  buf buffer_203 (buffer_203_out, buffer_202_out);
  buf buffer_204 (buffer_204_out, buffer_203_out);
  buf buffer_205 (buffer_205_out, buffer_204_out);
  and and_74 (DR3, DRR, d_ff_26_q);
  and and_75 (and_75_out, and_4_out, not_11_out, d_ff_25_q);
  D_Flip_Flop #(.trigger("high")) d_ff_37 (.D(and_75_out), .clk(and_5_out), .Q(d_ff_37_q));  // open: Qn, preset, reset
  and and_76 (and_76_out, and_6_out, not_11_out, d_ff_25_q);
  D_Flip_Flop #(.trigger("high")) d_ff_38 (.D(and_76_out), .clk(and_7_out), .Q(d_ff_38_q));  // open: Qn, preset, reset
  and and_77 (and_77_out, and_8_out, not_11_out, d_ff_25_q);
  D_Flip_Flop #(.trigger("high")) d_ff_39 (.D(and_77_out), .clk(and_9_out), .Q(d_ff_39_q));  // open: Qn, preset, reset
  and and_78 (and_78_out, and_10_out, not_11_out, d_ff_25_q);
  D_Flip_Flop #(.trigger("high")) d_ff_40 (.D(and_78_out), .clk(and_11_out), .Q(d_ff_40_q));  // open: Qn, preset, reset
  and and_79 (and_79_out, and_12_out, not_11_out, d_ff_25_q);
  D_Flip_Flop #(.trigger("high")) d_ff_41 (.D(and_79_out), .clk(and_13_out), .Q(d_ff_41_q));  // open: Qn, preset, reset
  and and_80 (and_80_out, and_14_out, not_11_out, d_ff_25_q);
  D_Flip_Flop #(.trigger("high")) d_ff_42 (.D(and_80_out), .clk(and_15_out), .Q(d_ff_42_q));  // open: Qn, preset, reset
  and and_81 (and_81_out, and_16_out, not_11_out, d_ff_25_q);
  D_Flip_Flop #(.trigger("high")) d_ff_43 (.D(and_81_out), .clk(and_17_out), .Q(d_ff_43_q));  // open: Qn, preset, reset
  and and_82 (and_82_out, and_18_out, not_11_out, d_ff_25_q);
  D_Flip_Flop #(.trigger("high")) d_ff_44 (.D(and_82_out), .clk(and_19_out), .Q(Display0));  // open: Qn, preset, reset
  buf buffer_206 (buffer_206_out, buffer_197_out);
  buf buffer_207 (buffer_207_out, buffer_206_out);
  buf buffer_208 (buffer_208_out, buffer_207_out);
  buf buffer_209 (buffer_209_out, buffer_210_out);
  buf buffer_210 (buffer_210_out, buffer_211_out);
  buf buffer_211 (buffer_211_out, buffer_215_out);
  buf buffer_212 (buffer_212_out, buffer_205_out);
  buf buffer_213 (buffer_213_out, buffer_212_out);
  buf buffer_214 (buffer_214_out, buffer_213_out);
  buf buffer_215 (buffer_215_out, buffer_214_out);
  and and_83 (DR2, DRR, d_ff_27_q);
  or or_4 (or_4_out, and_84_out, and_85_out, and_86_out, and_87_out, and_88_out, and_89_out, and_90_out, and_91_out);
  and and_84 (and_84_out, d_ff_37_q, and_4_out, d_ff_4_q);
  and and_85 (and_85_out, d_ff_38_q, and_6_out, d_ff_4_q);
  and and_86 (and_86_out, d_ff_39_q, and_8_out, d_ff_4_q);
  and and_87 (and_87_out, d_ff_40_q, and_10_out, d_ff_4_q);
  and and_88 (and_88_out, d_ff_41_q, and_12_out, d_ff_4_q);
  and and_89 (and_89_out, d_ff_42_q, and_14_out, d_ff_4_q);
  and and_90 (and_90_out, d_ff_43_q, and_16_out, d_ff_4_q);
  and and_91 (and_91_out, Display0, and_18_out, d_ff_4_q);
  and and_92 (DR1, DRR, d_ff_28_q);

  // Notes on the sheet:
  //   3-bit address input pins AR
  //   AR1
  //   Maybe do clock and enable pin here
  //   Mode input pin
  //   4-bit data input pins - DR
endmodule

module CU (
  input  i1,
  input  i2,
  input  in_3,
  input  i4,
  output IR1read,
  output IR2read,
  output IR3read,
  output IR4read,
  output MARwrite,
  output MARread,
  output MBRwrite,
  output MBRread,
  output ARwrite,
  output ARread,
  output DRwrite,
  output DRread,
  output RAMmode,
  output PCincr,
  output PCread,
  output IRwrite,
  output IRread,
  output out_22,
  output out_23,
  output out_24,
  output out_25,
  output Lwrite,
  output Lread,
  output Rwrite,
  output Rread,
  output Awrite,
  output Aread,
  output STATUSwrite,
  output STATUSread,
  output ALUmode,
  output CLOCKwrite
);

  wire and_1_out, and_2_out, and_3_out, and_4_out, and_5_out, and_6_out, and_7_out, and_8_out, and_9_out,
       and_10_out, and_11_out, and_12_out, and_13_out, and_14_out, and_15_out, and_16_out, and_17_out,
       and_18_out, and_19_out, and_20_out, and_21_out, and_22_out, and_23_out, and_24_out, and_25_out,
       and_26_out, and_27_out, and_28_out, and_29_out, and_30_out, and_31_out, and_32_out, and_33_out,
       and_34_out, and_35_out, and_36_out, and_37_out, and_38_out, and_39_out, and_40_out, clock_1_out,
       o00_out, o01_out, o10_out, o11_out, or_1_out, or_2_out, or_3_out, or_4_out, or_5_out, or_6_out,
       or_7_out, or_8_out, or_9_out, or_10_out, or_11_out, stepincrementor_1_s1, stepincrementor_1_s2,
       stepincrementor_1_s3, stepincrementor_1_s4;

  Clock clock_1 (.out(clock_1_out));
  and o00 (o00_out, ~i1, ~i2);  // AND_Gate
  and o01 (o01_out, ~i1, i2);  // AND_Gate
  and o10 (o10_out, i1, ~i2);  // AND_Gate
  and o11 (o11_out, i1, i2);
  or or_1 (or_1_out, o10_out, and_1_out);
  and and_1 (and_1_out, o11_out, ~i4);  // AND_Gate
  and and_2 (and_2_out, i4, o11_out);
  StepIncrementor stepincrementor_1 (
    .clock(clock_1_out), .s1(stepincrementor_1_s1), .s2(stepincrementor_1_s2), .s3(stepincrementor_1_s3),
    .s4(stepincrementor_1_s4));
  and and_3 (and_3_out, o00_out, stepincrementor_1_s1, ~stepincrementor_1_s2, stepincrementor_1_s3, ~stepincrementor_1_s4);  // AND_Gate
  and and_4 (and_4_out, o00_out, ~stepincrementor_1_s1, stepincrementor_1_s2, stepincrementor_1_s3, ~stepincrementor_1_s4);  // AND_Gate
  and and_5 (and_5_out, o00_out, stepincrementor_1_s1, stepincrementor_1_s2, stepincrementor_1_s3, ~stepincrementor_1_s4);  // AND_Gate
  and and_6 (and_6_out, o00_out, ~stepincrementor_1_s1, ~stepincrementor_1_s2, ~stepincrementor_1_s3, stepincrementor_1_s4);  // AND_Gate
  and and_7 (and_7_out, o00_out, stepincrementor_1_s1, ~stepincrementor_1_s2, ~stepincrementor_1_s3, stepincrementor_1_s4);  // AND_Gate
  and and_8 (and_8_out, o00_out, ~stepincrementor_1_s1, stepincrementor_1_s2, ~stepincrementor_1_s3, stepincrementor_1_s4);  // AND_Gate
  and and_9 (and_9_out, o00_out, ~stepincrementor_1_s1, ~stepincrementor_1_s2, ~stepincrementor_1_s3, ~stepincrementor_1_s4);  // AND_Gate
  and and_10 (and_10_out, o00_out, stepincrementor_1_s1, ~stepincrementor_1_s2, ~stepincrementor_1_s3, ~stepincrementor_1_s4);  // AND_Gate
  and and_11 (and_11_out, o00_out, ~stepincrementor_1_s1, stepincrementor_1_s2, ~stepincrementor_1_s3, ~stepincrementor_1_s4);  // AND_Gate
  and and_12 (and_12_out, o00_out, stepincrementor_1_s1, stepincrementor_1_s2, ~stepincrementor_1_s3, ~stepincrementor_1_s4);  // AND_Gate
  and and_13 (and_13_out, o00_out, ~stepincrementor_1_s1, ~stepincrementor_1_s2, stepincrementor_1_s3, ~stepincrementor_1_s4);  // AND_Gate
  and and_14 (and_14_out, o01_out, stepincrementor_1_s1, ~stepincrementor_1_s2, stepincrementor_1_s3, ~stepincrementor_1_s4);  // AND_Gate
  and and_15 (and_15_out, o01_out, ~stepincrementor_1_s1, stepincrementor_1_s2, stepincrementor_1_s3, ~stepincrementor_1_s4);  // AND_Gate
  and and_16 (and_16_out, o01_out, stepincrementor_1_s1, stepincrementor_1_s2, stepincrementor_1_s3, ~stepincrementor_1_s4);  // AND_Gate
  and and_17 (and_17_out, o01_out, ~stepincrementor_1_s1, ~stepincrementor_1_s2, ~stepincrementor_1_s3, stepincrementor_1_s4);  // AND_Gate
  and and_18 (and_18_out, o01_out, stepincrementor_1_s1, ~stepincrementor_1_s2, ~stepincrementor_1_s3, stepincrementor_1_s4);  // AND_Gate
  and and_19 (and_19_out, o01_out, ~stepincrementor_1_s1, stepincrementor_1_s2, ~stepincrementor_1_s3, stepincrementor_1_s4);  // AND_Gate
  and and_20 (and_20_out, o01_out, ~stepincrementor_1_s1, ~stepincrementor_1_s2, ~stepincrementor_1_s3, ~stepincrementor_1_s4);  // AND_Gate
  and and_21 (and_21_out, o01_out, stepincrementor_1_s1, ~stepincrementor_1_s2, ~stepincrementor_1_s3, ~stepincrementor_1_s4);  // AND_Gate
  and and_22 (and_22_out, o01_out, ~stepincrementor_1_s1, stepincrementor_1_s2, ~stepincrementor_1_s3, ~stepincrementor_1_s4);  // AND_Gate
  and and_23 (and_23_out, o01_out, stepincrementor_1_s1, stepincrementor_1_s2, ~stepincrementor_1_s3, ~stepincrementor_1_s4);  // AND_Gate
  and and_24 (and_24_out, o01_out, ~stepincrementor_1_s1, ~stepincrementor_1_s2, stepincrementor_1_s3, ~stepincrementor_1_s4);  // AND_Gate
  and and_25 (and_25_out, or_1_out, stepincrementor_1_s1, ~stepincrementor_1_s2, stepincrementor_1_s3, ~stepincrementor_1_s4);  // AND_Gate
  and and_26 (and_26_out, or_1_out, ~stepincrementor_1_s1, stepincrementor_1_s2, stepincrementor_1_s3, ~stepincrementor_1_s4);  // AND_Gate
  and and_27 (and_27_out, or_1_out, stepincrementor_1_s1, stepincrementor_1_s2, stepincrementor_1_s3, ~stepincrementor_1_s4);  // AND_Gate
  and and_28 (and_28_out, or_1_out, ~stepincrementor_1_s1, ~stepincrementor_1_s2, ~stepincrementor_1_s3, stepincrementor_1_s4);  // AND_Gate
  and and_29 (and_29_out, or_1_out, stepincrementor_1_s1, ~stepincrementor_1_s2, ~stepincrementor_1_s3, stepincrementor_1_s4);  // AND_Gate
  and and_30 (and_30_out, or_1_out, ~stepincrementor_1_s1, stepincrementor_1_s2, ~stepincrementor_1_s3, stepincrementor_1_s4);  // AND_Gate
  and and_31 (and_31_out, or_1_out, ~stepincrementor_1_s1, ~stepincrementor_1_s2, ~stepincrementor_1_s3, ~stepincrementor_1_s4);  // AND_Gate
  and and_32 (and_32_out, or_1_out, stepincrementor_1_s1, ~stepincrementor_1_s2, ~stepincrementor_1_s3, ~stepincrementor_1_s4);  // AND_Gate
  and and_33 (and_33_out, or_1_out, ~stepincrementor_1_s1, stepincrementor_1_s2, ~stepincrementor_1_s3, ~stepincrementor_1_s4);  // AND_Gate
  and and_34 (and_34_out, or_1_out, stepincrementor_1_s1, stepincrementor_1_s2, ~stepincrementor_1_s3, ~stepincrementor_1_s4);  // AND_Gate
  and and_35 (and_35_out, or_1_out, ~stepincrementor_1_s1, ~stepincrementor_1_s2, stepincrementor_1_s3, ~stepincrementor_1_s4);  // AND_Gate
  or or_2 (or_2_out, and_8_out, and_19_out, and_30_out);
  or or_3 (or_3_out, and_9_out, and_20_out, and_31_out);
  or or_4 (or_4_out, and_10_out, and_21_out, and_32_out);
  or or_5 (or_5_out, and_11_out, and_22_out, and_33_out);
  or or_6 (or_6_out, and_12_out, and_23_out, and_34_out);
  or or_7 (or_7_out, and_13_out, and_24_out, and_35_out);
  and and_36 (and_36_out, and_27_out, and_1_out);
  buf or_8 (or_8_out, and_7_out);  // OR_Gate
  and and_37 (and_37_out, or_8_out, ~in_3);  // AND_Gate
  or or_9 (or_9_out, and_26_out, and_14_out);
  and and_38 (and_38_out, or_9_out, ~in_3);  // AND_Gate
  buf or_10 (or_10_out, and_7_out);  // OR_Gate
  and and_39 (and_39_out, or_10_out, in_3);
  or or_11 (or_11_out, and_26_out, and_14_out);
  and and_40 (and_40_out, or_11_out, in_3);
  // OR_Gate or_12 has open pins: out=IR1read
  // OR_Gate or_13 has open pins: out=IR2read
  // OR_Gate or_14 has open pins: out=IR3read
  or or_15 (IR4read, and_15_out, and_3_out);
  or or_16 (MARwrite, and_3_out, or_3_out, and_15_out);
  or or_17 (MARread, and_4_out, or_4_out, and_17_out);
  or or_18 (MBRwrite, and_6_out, or_6_out, and_14_out);
  or or_19 (MBRread, and_7_out, or_7_out, and_16_out);
  or or_20 (ARwrite, and_4_out, or_4_out, and_17_out);
  or or_21 (ARread, and_5_out, or_5_out, and_18_out);
  or or_22 (DRwrite, and_18_out, and_16_out);
  or or_23 (DRread, and_6_out, or_5_out, or_6_out);
  or or_24 (RAMmode, and_5_out, or_6_out, and_6_out, or_7_out, or_5_out);
  buf or_25 (PCincr, or_2_out);  // OR_Gate
  or or_26 (PCread, or_3_out, or_2_out, or_4_out);
  buf or_27 (IRwrite, or_7_out);  // OR_Gate
  buf or_28 (IRread, 1'b0);  // OR_Gate
  or or_29 (out_22, and_37_out, and_28_out);
  or or_30 (out_23, and_38_out, and_25_out);
  buf or_31 (out_24, and_39_out);  // OR_Gate
  buf or_32 (out_25, and_40_out);  // OR_Gate
  buf or_33 (Lwrite, and_25_out);  // OR_Gate
  buf or_34 (Lread, and_27_out);  // OR_Gate
  buf or_35 (Rwrite, and_26_out);  // OR_Gate
  buf or_36 (Rread, and_27_out);  // OR_Gate
  buf or_37 (Awrite, and_27_out);  // OR_Gate
  buf or_38 (Aread, and_28_out);  // OR_Gate
  buf or_39 (STATUSwrite, and_27_out);  // OR_Gate
  buf or_40 (STATUSread, 1'b0);  // OR_Gate
  buf or_41 (ALUmode, and_36_out);  // OR_Gate
  buf or_42 (CLOCKwrite, and_2_out);  // OR_Gate
endmodule

module Reg4Bit (
  input  d3,
  input  d2,
  input  d1,
  input  d0,
  input  en,
  input  clk,
  input  rw,
  output b3,
  output b2,
  output b1,
  output b0
);

  wire and_1_out, buffer_1_out, buffer_2_out, buffer_3_out, buffer_4_out, buffer_5_out, buffer_6_out,
       buffer_7_out, buffer_8_out, buffer_9_out, buffer_10_out, buffer_11_out, buffer_12_out, buffer_13_out,
       buffer_14_out, buffer_15_out, buffer_16_out, buffer_17_out, buffer_18_out, buffer_19_out,
       buffer_20_out, buffer_21_out, buffer_22_out, buffer_23_out, buffer_24_out, buffer_25_out,
       buffer_26_out, buffer_27_out, buffer_28_out, buffer_29_out, buffer_30_out, buffer_31_out,
       buffer_32_out, buffer_33_out, buffer_34_out, buffer_35_out, buffer_36_out, buffer_37_out,
       buffer_38_out, buffer_39_out, buffer_40_out, buffer_41_out, buffer_42_out, buffer_43_out,
       buffer_44_out, buffer_45_out, buffer_46_out, buffer_47_out, buffer_48_out, buffer_49_out,
       buffer_50_out, buffer_51_out, buffer_52_out, buffer_53_out, buffer_54_out, buffer_55_out,
       buffer_56_out, buffer_57_out, buffer_58_out, buffer_59_out, buffer_60_out, buffer_61_out,
       buffer_62_out, buffer_63_out, buffer_64_out, buffer_65_out, buffer_66_out, buffer_67_out,
       buffer_68_out, buffer_69_out, buffer_70_out, buffer_71_out, buffer_72_out, buffer_73_out,
       buffer_74_out, buffer_75_out, buffer_76_out, buffer_77_out, buffer_78_out, buffer_79_out,
       buffer_80_out, buffer_81_out, buffer_82_out, buffer_83_out, buffer_84_out, buffer_85_out,
       buffer_86_out, buffer_87_out, buffer_88_out, buffer_89_out, buffer_90_out, buffer_91_out,
       buffer_92_out, buffer_93_out, buffer_94_out, buffer_95_out, buffer_96_out, buffer_97_out,
       buffer_98_out, buffer_99_out, buffer_100_out, buffer_101_out, buffer_102_out, buffer_103_out,
       buffer_104_out, buffer_105_out, buffer_106_out, buffer_107_out, buffer_108_out, buffer_109_out,
       buffer_110_out, buffer_111_out, buffer_112_out, buffer_113_out, buffer_114_out, buffer_115_out,
       buffer_116_out, buffer_117_out, buffer_118_out, buffer_119_out, buffer_120_out, buffer_121_out,
       buffer_122_out, buffer_123_out, buffer_124_out, buffer_125_out, buffer_126_out, buffer_127_out,
       buffer_128_out, buffer_129_out, buffer_130_out, buffer_131_out, buffer_132_out, buffer_133_out,
       buffer_134_out, buffer_135_out, buffer_136_out, buffer_137_out, buffer_138_out, buffer_139_out,
       buffer_140_out, buffer_141_out, buffer_142_out, buffer_143_out, buffer_144_out, buffer_145_out,
       buffer_146_out, buffer_147_out, buffer_148_out, buffer_149_out, buffer_150_out, buffer_151_out,
       buffer_152_out, buffer_153_out, buffer_154_out, buffer_155_out, buffer_156_out, buffer_157_out,
       buffer_158_out, buffer_159_out, buffer_160_out, buffer_161_out, buffer_162_out, buffer_163_out,
       buffer_164_out, buffer_165_out, buffer_166_out, buffer_167_out, buffer_168_out, buffer_169_out,
       buffer_170_out, buffer_171_out, buffer_172_out, buffer_173_out, buffer_174_out, buffer_175_out,
       buffer_176_out, buffer_177_out, buffer_178_out, buffer_179_out, buffer_180_out, buffer_181_out,
       buffer_182_out, buffer_183_out, buffer_184_out, buffer_185_out, buffer_186_out, buffer_187_out,
       buffer_188_out, buffer_189_out, buffer_190_out, buffer_191_out, buffer_192_out, buffer_193_out,
       buffer_194_out, buffer_195_out, buffer_196_out, buffer_197_out, buffer_198_out, buffer_199_out,
       buffer_200_out, buffer_201_out, buffer_202_out, buffer_203_out, buffer_204_out, buffer_205_out,
       buffer_206_out, buffer_207_out, buffer_208_out, buffer_209_out, buffer_210_out, buffer_211_out,
       d_ff_1_q, d_ff_2_q, d_ff_3_q, d_ff_4_q;

  buf buffer_1 (buffer_1_out, buffer_3_out);
  buf buffer_2 (buffer_2_out, buffer_12_out);
  buf buffer_3 (buffer_3_out, buffer_5_out);
  buf buffer_4 (buffer_4_out, buffer_2_out);
  buf buffer_5 (buffer_5_out, buffer_7_out);
  buf buffer_6 (buffer_6_out, buffer_4_out);
  buf buffer_7 (buffer_7_out, clk);
  buf buffer_8 (buffer_8_out, buffer_6_out);
  buf buffer_9 (buffer_9_out, buffer_8_out);
  buf buffer_10 (buffer_10_out, buffer_9_out);
  buf buffer_11 (buffer_11_out, buffer_10_out);
  buf buffer_12 (buffer_12_out, buffer_13_out);
  buf buffer_13 (buffer_13_out, buffer_14_out);
  buf buffer_14 (buffer_14_out, buffer_15_out);
  buf buffer_15 (buffer_15_out, buffer_26_out);
  buf buffer_16 (buffer_16_out, buffer_19_out);
  buf buffer_17 (buffer_17_out, buffer_16_out);
  buf buffer_18 (buffer_18_out, buffer_17_out);
  buf buffer_19 (buffer_19_out, buffer_20_out);
  buf buffer_20 (buffer_20_out, buffer_21_out);
  buf buffer_21 (buffer_21_out, buffer_22_out);
  buf buffer_22 (buffer_22_out, buffer_34_out);
  buf buffer_23 (buffer_23_out, buffer_1_out);
  buf buffer_24 (buffer_24_out, buffer_23_out);
  buf buffer_25 (buffer_25_out, buffer_24_out);
  and and_1 (and_1_out, buffer_11_out, rw);
  buf buffer_26 (buffer_26_out, buffer_27_out);
  buf buffer_27 (buffer_27_out, buffer_28_out);
  buf buffer_28 (buffer_28_out, buffer_29_out);
  buf buffer_29 (buffer_29_out, buffer_42_out);
  buf buffer_30 (buffer_30_out, buffer_18_out);
  buf buffer_31 (buffer_31_out, buffer_30_out);
  buf buffer_32 (buffer_32_out, buffer_31_out);
  buf buffer_33 (buffer_33_out, buffer_32_out);
  buf buffer_34 (buffer_34_out, buffer_35_out);
  buf buffer_35 (buffer_35_out, buffer_36_out);
  buf buffer_36 (buffer_36_out, buffer_37_out);
  buf buffer_37 (buffer_37_out, buffer_50_out);
  buf buffer_38 (buffer_38_out, buffer_25_out);
  buf buffer_39 (buffer_39_out, buffer_38_out);
  buf buffer_40 (buffer_40_out, buffer_39_out);
  buf buffer_41 (buffer_41_out, buffer_40_out);
  D_Flip_Flop d_ff_1 (.D(d0), .clk(and_1_out), .Q(d_ff_1_q));  // open: Qn, preset, reset
  D_Flip_Flop d_ff_2 (.D(d1), .clk(and_1_out), .Q(d_ff_2_q));  // open: Qn, preset, reset
  D_Flip_Flop d_ff_3 (.D(d2), .clk(and_1_out), .Q(d_ff_3_q));  // open: Qn, preset, reset
  D_Flip_Flop d_ff_4 (.D(d3), .clk(and_1_out), .Q(d_ff_4_q));  // open: Qn, preset, reset
  buf buffer_42 (buffer_42_out, buffer_43_out);
  buf buffer_43 (buffer_43_out, buffer_44_out);
  buf buffer_44 (buffer_44_out, buffer_45_out);
  buf buffer_45 (buffer_45_out, buffer_58_out);
  buf buffer_46 (buffer_46_out, buffer_33_out);
  buf buffer_47 (buffer_47_out, buffer_46_out);
  buf buffer_48 (buffer_48_out, buffer_47_out);
  buf buffer_49 (buffer_49_out, buffer_48_out);
  buf buffer_50 (buffer_50_out, buffer_51_out);
  buf buffer_51 (buffer_51_out, buffer_52_out);
  buf buffer_52 (buffer_52_out, buffer_53_out);
  buf buffer_53 (buffer_53_out, buffer_66_out);
  buf buffer_54 (buffer_54_out, buffer_41_out);
  buf buffer_55 (buffer_55_out, buffer_54_out);
  buf buffer_56 (buffer_56_out, buffer_55_out);
  buf buffer_57 (buffer_57_out, buffer_56_out);
  buf buffer_58 (buffer_58_out, buffer_59_out);
  buf buffer_59 (buffer_59_out, buffer_60_out);
  buf buffer_60 (buffer_60_out, buffer_61_out);
  buf buffer_61 (buffer_61_out, buffer_74_out);
  buf buffer_62 (buffer_62_out, buffer_49_out);
  buf buffer_63 (buffer_63_out, buffer_62_out);
  buf buffer_64 (buffer_64_out, buffer_63_out);
  buf buffer_65 (buffer_65_out, buffer_64_out);
  buf buffer_66 (buffer_66_out, buffer_67_out);
  buf buffer_67 (buffer_67_out, buffer_68_out);
  buf buffer_68 (buffer_68_out, buffer_69_out);
  buf buffer_69 (buffer_69_out, buffer_82_out);
  buf buffer_70 (buffer_70_out, buffer_57_out);
  buf buffer_71 (buffer_71_out, buffer_70_out);
  buf buffer_72 (buffer_72_out, buffer_71_out);
  buf buffer_73 (buffer_73_out, buffer_72_out);
  and and_2 (b0, en, d_ff_1_q);
  and and_3 (b1, en, d_ff_2_q);
  and and_4 (b2, en, d_ff_3_q);
  and and_5 (b3, en, d_ff_4_q);
  buf buffer_74 (buffer_74_out, buffer_75_out);
  buf buffer_75 (buffer_75_out, buffer_76_out);
  buf buffer_76 (buffer_76_out, buffer_77_out);
  buf buffer_77 (buffer_77_out, buffer_90_out);
  buf buffer_78 (buffer_78_out, buffer_65_out);
  buf buffer_79 (buffer_79_out, buffer_78_out);
  buf buffer_80 (buffer_80_out, buffer_79_out);
  buf buffer_81 (buffer_81_out, buffer_80_out);
  buf buffer_82 (buffer_82_out, buffer_83_out);
  buf buffer_83 (buffer_83_out, buffer_84_out);
  buf buffer_84 (buffer_84_out, buffer_85_out);
  buf buffer_85 (buffer_85_out, buffer_98_out);
  buf buffer_86 (buffer_86_out, buffer_73_out);
  buf buffer_87 (buffer_87_out, buffer_86_out);
  buf buffer_88 (buffer_88_out, buffer_87_out);
  buf buffer_89 (buffer_89_out, buffer_88_out);
  buf buffer_90 (buffer_90_out, buffer_91_out);
  buf buffer_91 (buffer_91_out, buffer_92_out);
  buf buffer_92 (buffer_92_out, buffer_93_out);
  buf buffer_93 (buffer_93_out, buffer_106_out);
  buf buffer_94 (buffer_94_out, buffer_81_out);
  buf buffer_95 (buffer_95_out, buffer_94_out);
  buf buffer_96 (buffer_96_out, buffer_95_out);
  buf buffer_97 (buffer_97_out, buffer_96_out);
  buf buffer_98 (buffer_98_out, buffer_99_out);
  buf buffer_99 (buffer_99_out, buffer_100_out);
  buf buffer_100 (buffer_100_out, buffer_101_out);
  buf buffer_101 (buffer_101_out, buffer_114_out);
  buf buffer_102 (buffer_102_out, buffer_89_out);
  buf buffer_103 (buffer_103_out, buffer_102_out);
  buf buffer_104 (buffer_104_out, buffer_103_out);
  buf buffer_105 (buffer_105_out, buffer_104_out);
  buf buffer_106 (buffer_106_out, buffer_107_out);
  buf buffer_107 (buffer_107_out, buffer_108_out);
  buf buffer_108 (buffer_108_out, buffer_109_out);
  buf buffer_109 (buffer_109_out, buffer_124_out);
  buf buffer_110 (buffer_110_out, buffer_97_out);
  buf buffer_111 (buffer_111_out, buffer_110_out);
  buf buffer_112 (buffer_112_out, buffer_111_out);
  buf buffer_113 (buffer_113_out, buffer_112_out);
  buf buffer_114 (buffer_114_out, buffer_115_out);
  buf buffer_115 (buffer_115_out, buffer_116_out);
  buf buffer_116 (buffer_116_out, buffer_117_out);
  buf buffer_117 (buffer_117_out, buffer_132_out);
  buf buffer_118 (buffer_118_out, buffer_105_out);
  buf buffer_119 (buffer_119_out, buffer_118_out);
  buf buffer_120 (buffer_120_out, buffer_119_out);
  buf buffer_121 (buffer_121_out, buffer_120_out);
  buf buffer_122 (buffer_122_out, buffer_123_out);
  buf buffer_123 (buffer_123_out, buffer_138_out);
  buf buffer_124 (buffer_124_out, buffer_125_out);
  buf buffer_125 (buffer_125_out, buffer_122_out);
  buf buffer_126 (buffer_126_out, buffer_129_out);
  buf buffer_127 (buffer_127_out, buffer_126_out);
  buf buffer_128 (buffer_128_out, buffer_113_out);
  buf buffer_129 (buffer_129_out, buffer_128_out);
  buf buffer_130 (buffer_130_out, buffer_131_out);
  buf buffer_131 (buffer_131_out, buffer_146_out);
  buf buffer_132 (buffer_132_out, buffer_133_out);
  buf buffer_133 (buffer_133_out, buffer_130_out);
  buf buffer_134 (buffer_134_out, buffer_137_out);
  buf buffer_135 (buffer_135_out, buffer_134_out);
  buf buffer_136 (buffer_136_out, buffer_121_out);
  buf buffer_137 (buffer_137_out, buffer_136_out);
  buf buffer_138 (buffer_138_out, buffer_139_out);
  buf buffer_139 (buffer_139_out, buffer_140_out);
  buf buffer_140 (buffer_140_out, buffer_141_out);
  buf buffer_141 (buffer_141_out, buffer_154_out);
  buf buffer_142 (buffer_142_out, buffer_127_out);
  buf buffer_143 (buffer_143_out, buffer_142_out);
  buf buffer_144 (buffer_144_out, buffer_143_out);
  buf buffer_145 (buffer_145_out, buffer_144_out);
  buf buffer_146 (buffer_146_out, buffer_147_out);
  buf buffer_147 (buffer_147_out, buffer_148_out);
  buf buffer_148 (buffer_148_out, buffer_149_out);
  buf buffer_149 (buffer_149_out, buffer_162_out);
  buf buffer_150 (buffer_150_out, buffer_135_out);
  buf buffer_151 (buffer_151_out, buffer_150_out);
  buf buffer_152 (buffer_152_out, buffer_151_out);
  buf buffer_153 (buffer_153_out, buffer_152_out);
  buf buffer_154 (buffer_154_out, buffer_155_out);
  buf buffer_155 (buffer_155_out, buffer_156_out);
  buf buffer_156 (buffer_156_out, buffer_157_out);
  buf buffer_157 (buffer_157_out, buffer_170_out);
  buf buffer_158 (buffer_158_out, buffer_145_out);
  buf buffer_159 (buffer_159_out, buffer_158_out);
  buf buffer_160 (buffer_160_out, buffer_159_out);
  buf buffer_161 (buffer_161_out, buffer_160_out);
  buf buffer_162 (buffer_162_out, buffer_163_out);
  buf buffer_163 (buffer_163_out, buffer_164_out);
  buf buffer_164 (buffer_164_out, buffer_165_out);
  buf buffer_165 (buffer_165_out, buffer_178_out);
  buf buffer_166 (buffer_166_out, buffer_153_out);
  buf buffer_167 (buffer_167_out, buffer_166_out);
  buf buffer_168 (buffer_168_out, buffer_167_out);
  buf buffer_169 (buffer_169_out, buffer_168_out);
  buf buffer_170 (buffer_170_out, buffer_171_out);
  buf buffer_171 (buffer_171_out, buffer_172_out);
  buf buffer_172 (buffer_172_out, buffer_173_out);
  buf buffer_173 (buffer_173_out, buffer_186_out);
  buf buffer_174 (buffer_174_out, buffer_161_out);
  buf buffer_175 (buffer_175_out, buffer_174_out);
  buf buffer_176 (buffer_176_out, buffer_175_out);
  buf buffer_177 (buffer_177_out, buffer_176_out);
  buf buffer_178 (buffer_178_out, buffer_179_out);
  buf buffer_179 (buffer_179_out, buffer_180_out);
  buf buffer_180 (buffer_180_out, buffer_181_out);
  buf buffer_181 (buffer_181_out, buffer_194_out);
  buf buffer_182 (buffer_182_out, buffer_169_out);
  buf buffer_183 (buffer_183_out, buffer_182_out);
  buf buffer_184 (buffer_184_out, buffer_183_out);
  buf buffer_185 (buffer_185_out, buffer_184_out);
  buf buffer_186 (buffer_186_out, buffer_187_out);
  buf buffer_187 (buffer_187_out, buffer_188_out);
  buf buffer_188 (buffer_188_out, buffer_189_out);
  buf buffer_189 (buffer_189_out, buffer_202_out);
  buf buffer_190 (buffer_190_out, buffer_177_out);
  buf buffer_191 (buffer_191_out, buffer_190_out);
  buf buffer_192 (buffer_192_out, buffer_191_out);
  buf buffer_193 (buffer_193_out, buffer_192_out);
  buf buffer_194 (buffer_194_out, buffer_195_out);
  buf buffer_195 (buffer_195_out, buffer_196_out);
  buf buffer_196 (buffer_196_out, buffer_197_out);
  buf buffer_197 (buffer_197_out, buffer_207_out);
  buf buffer_198 (buffer_198_out, buffer_185_out);
  buf buffer_199 (buffer_199_out, buffer_198_out);
  buf buffer_200 (buffer_200_out, buffer_199_out);
  buf buffer_201 (buffer_201_out, buffer_200_out);
  buf buffer_202 (buffer_202_out, buffer_203_out);
  buf buffer_203 (buffer_203_out, buffer_206_out);
  buf buffer_204 (buffer_204_out, buffer_193_out);
  buf buffer_205 (buffer_205_out, buffer_204_out);
  buf buffer_206 (buffer_206_out, buffer_205_out);
  buf buffer_207 (buffer_207_out, buffer_208_out);
  buf buffer_208 (buffer_208_out, buffer_211_out);
  buf buffer_209 (buffer_209_out, buffer_201_out);
  buf buffer_210 (buffer_210_out, buffer_209_out);
  buf buffer_211 (buffer_211_out, buffer_210_out);

  // Notes on the sheet:
  //   Input
  //   1 = write
  //   0 = read
  //   Output
  //   Output
  //   Output
  //   Output
endmodule

module StepIncrementor (
  input  clock,
  output s1,
  output s2,
  output s3,
  output s4
);

  wire and_1_out, and_2_out, and_3_out, and_4_out, and_5_out, and_6_out, and_7_out, and_8_out, and_9_out,
       and_10_out, and_11_out, and_12_out, and_13_out, not_1_out, not_2_out, not_3_out, not_4_out, not_5_out,
       or_1_out, or_2_out, or_3_out, or_4_out;

  D_Flip_Flop d_ff_1 (.D(and_13_out), .clk(clock), .Q(s1));  // open: Qn, preset, reset
  D_Flip_Flop d_ff_2 (.D(and_9_out), .clk(clock), .Q(s2));  // open: Qn, preset, reset
  D_Flip_Flop d_ff_3 (.D(and_6_out), .clk(clock), .Q(s3));  // open: Qn, preset, reset
  D_Flip_Flop d_ff_4 (.D(and_3_out), .clk(clock), .Q(s4));  // open: Qn, preset, reset
  not not_1 (not_1_out, clock);
  and and_1 (and_1_out, and_2_out, and_4_out);
  and and_2 (and_2_out, s4, not_1_out);
  or or_1 (or_1_out, and_2_out, and_4_out);
  not not_2 (not_2_out, and_1_out);
  and and_3 (and_3_out, not_2_out, or_1_out);
  and and_4 (and_4_out, and_5_out, and_7_out);
  not not_3 (not_3_out, and_4_out);
  and and_5 (and_5_out, s3, not_1_out);
  or or_2 (or_2_out, and_5_out, and_7_out);
  and and_6 (and_6_out, not_3_out, or_2_out);
  and and_7 (and_7_out, and_8_out, and_10_out);
  and and_8 (and_8_out, s2, not_1_out);
  or or_3 (or_3_out, and_8_out, and_10_out);
  not not_4 (not_4_out, and_7_out);
  and and_9 (and_9_out, not_4_out, or_3_out);
  and and_10 (and_10_out, and_11_out, and_12_out);
  not not_5 (not_5_out, and_10_out);
  and and_11 (and_11_out, s1, not_1_out);
  and and_12 (and_12_out, 1'b1, not_1_out);
  or or_4 (or_4_out, and_11_out, and_12_out);
  and and_13 (and_13_out, not_5_out, or_4_out);
endmodule

module FillAdder (
  input  A,
  input  B,
  input  Carry,
  output C,
  output Sum
);

  wire and_1_out, and_2_out, xor_1_out;

  and and_1 (and_1_out, A, B);
  xor xor_1 (xor_1_out, A, B);
  and and_2 (and_2_out, xor_1_out, Carry);
  or or_1 (C, and_1_out, and_2_out);
  xor xor_2 (Sum, xor_1_out, Carry);
endmodule

module NewALU (
  input  L4,
  input  L3,
  input  L2,
  input  L1,
  input  R4,
  input  R3,
  input  R2,
  input  R1,
  input  mode,
  input  clock,
  output signed_overflow,
  output negative,
  output zero,
  output overflow,
  output A4,
  output A3,
  output A2,
  output A1
);

  wire and_1_out, and_2_out, and_3_out, and_4_out, and_5_out, and_6_out, and_7_out, and_8_out, and_9_out,
       and_10_out, and_11_out, and_12_out, and_13_out, and_14_out, and_15_out, and_16_out, and_17_out,
       and_18_out, and_19_out, and_20_out, and_22_out, and_23_out, and_24_out, and_25_out, and_26_out,
       and_27_out, and_28_out, and_29_out, and_30_out, and_31_out, and_32_out, and_33_out, and_34_out,
       and_35_out, and_36_out, and_37_out, and_38_out, and_39_out, not_2_out, not_3_out, not_4_out,
       not_5_out, not_6_out, not_7_out, not_8_out, not_9_out, or_2_out, or_4_out, or_5_out, or_7_out,
       or_8_out, or_10_out, or_11_out, or_12_out, or_13_out, or_15_out, or_16_out, xor_1_out, xor_2_out,
       xor_3_out, xor_4_out;

  and and_1 (and_1_out, and_2_out, and_25_out);
  and and_2 (and_2_out, clock, L4);
  and and_3 (and_3_out, and_2_out, or_4_out);
  and and_4 (and_4_out, and_25_out, or_4_out);
  or or_1 (overflow, and_1_out, and_3_out, and_4_out);
  or or_2 (or_2_out, and_2_out, and_25_out, or_4_out);
  and and_5 (and_5_out, ~overflow, or_2_out);  // AND_Gate
  and and_6 (and_6_out, and_2_out, and_25_out, or_4_out);
  or or_3 (A4, and_5_out, and_6_out);
  and and_7 (and_7_out, and_8_out, and_32_out);
  and and_8 (and_8_out, clock, L3);
  and and_9 (and_9_out, and_8_out, or_7_out);
  and and_10 (and_10_out, and_32_out, or_7_out);
  or or_4 (or_4_out, and_7_out, and_9_out, and_10_out);
  or or_5 (or_5_out, and_8_out, and_32_out, or_7_out);
  and and_11 (and_11_out, ~or_4_out, or_5_out);  // AND_Gate
  and and_12 (and_12_out, and_8_out, and_32_out, or_7_out);
  or or_6 (A3, and_11_out, and_12_out);
  and and_13 (and_13_out, and_14_out, and_35_out);
  and and_14 (and_14_out, clock, L2);
  and and_15 (and_15_out, and_14_out, and_19_out);
  and and_16 (and_16_out, and_35_out, and_19_out);
  or or_7 (or_7_out, and_13_out, and_15_out, and_16_out);
  or or_8 (or_8_out, and_14_out, and_35_out, and_19_out);
  and and_17 (and_17_out, ~or_7_out, or_8_out);  // AND_Gate
  and and_18 (and_18_out, and_14_out, and_35_out, and_19_out);
  or or_9 (A2, and_17_out, and_18_out);
  and and_19 (and_19_out, and_39_out, and_20_out);
  and and_20 (and_20_out, clock, L1);
  or or_10 (or_10_out, and_39_out, and_20_out);
  and and_21 (A1, ~and_19_out, or_10_out);  // AND_Gate
  or or_11 (or_11_out, A1, A2, A3, A4);
  and and_22 (and_22_out, clock, R4);
  not not_1 (zero, or_11_out);
  and and_23 (and_23_out, and_24_out, and_30_out);
  not not_2 (not_2_out, and_2_out);
  not not_3 (not_3_out, mode);
  not not_4 (not_4_out, and_22_out);
  not not_5 (not_5_out, mode);
  not not_6 (not_6_out, A4);
  not not_7 (not_7_out, and_2_out);
  not not_8 (not_8_out, and_22_out);
  not not_9 (not_9_out, A4);
  xor xor_1 (xor_1_out, mode, R4);
  and and_24 (and_24_out, clock, xor_1_out);
  or or_12 (or_12_out, and_24_out, and_30_out);
  and and_25 (and_25_out, ~and_23_out, or_12_out);  // AND_Gate
  and and_26 (and_26_out, not_2_out, not_3_out, not_4_out, A4);
  and and_27 (and_27_out, and_2_out, not_5_out, and_22_out, not_6_out);
  and and_28 (and_28_out, not_7_out, mode, and_22_out, A4);
  and and_29 (and_29_out, and_2_out, mode, not_8_out, not_9_out);
  and and_30 (and_30_out, and_31_out, and_33_out);
  xor xor_2 (xor_2_out, mode, R3);
  and and_31 (and_31_out, clock, xor_2_out);
  or or_13 (or_13_out, and_31_out, and_33_out);
  and and_32 (and_32_out, ~and_30_out, or_13_out);  // AND_Gate
  or or_14 (signed_overflow, and_26_out, and_27_out, and_28_out, and_29_out);
  and and_33 (and_33_out, and_34_out, and_36_out);
  xor xor_3 (xor_3_out, mode, R2);
  and and_34 (and_34_out, clock, xor_3_out);
  or or_15 (or_15_out, and_34_out, and_36_out);
  and and_35 (and_35_out, ~and_33_out, or_15_out);  // AND_Gate
  and and_36 (and_36_out, and_37_out, and_38_out);
  xor xor_4 (xor_4_out, mode, R1);
  and and_37 (and_37_out, clock, xor_4_out);
  and and_38 (and_38_out, clock, mode);
  or or_16 (or_16_out, and_37_out, and_38_out);
  and and_39 (and_39_out, ~and_36_out, or_16_out);  // AND_Gate

  assign negative = A4;

  // Notes on the sheet:
  //   clock
  //   adder
  //   Timofey Galyanov 261035970
  //   L input
  //   A-out
  //   status determination
  //   R input
  //   2's complement
endmodule

module calculationcirc (
  input  D3,
  input  D2,
  input  D1,
  input  D0,
  output B1,
  output BL1,
  output BR1,
  output M1,
  output TL1,
  output TR1,
  output T1,
  output B2,
  output BL2,
  output BR2,
  output M2,
  output TL2,
  output TR2,
  output T2
);

  wire or_1_out, or_2_out, or_3_out, or_4_out, or_5_out, or_6_out, or_7_out, s0_out, s1_out, s2_out, s3_out,
       s4_out, s5_out, s6_out, s7_out, s8_out, s9_out, s10_out, s11_out, s12_out, s13_out, s14_out, s15_out;

  and s0 (s0_out, ~D0, ~D1, ~D2, ~D3);  // AND_Gate
  and s1 (s1_out, D0, ~D1, ~D2, ~D3);  // AND_Gate
  and s2 (s2_out, ~D0, D1, ~D2, ~D3);  // AND_Gate
  and s3 (s3_out, D0, D1, ~D2, ~D3);  // AND_Gate
  and s4 (s4_out, ~D0, ~D1, D2, ~D3);  // AND_Gate
  and s5 (s5_out, D0, ~D1, D2, ~D3);  // AND_Gate
  and s6 (s6_out, ~D0, D1, D2, ~D3);  // AND_Gate
  and s7 (s7_out, D0, D1, D2, ~D3);  // AND_Gate
  and s8 (s8_out, ~D0, ~D1, ~D2, D3);  // AND_Gate
  and s9 (s9_out, D0, ~D1, ~D2, D3);  // AND_Gate
  and s10 (s10_out, ~D0, D1, ~D2, D3);  // AND_Gate
  and s11 (s11_out, D0, D1, ~D2, D3);  // AND_Gate
  and s12 (s12_out, ~D0, ~D1, D2, D3);  // AND_Gate
  and s13 (s13_out, D0, ~D1, D2, D3);  // AND_Gate
  and s14 (s14_out, ~D0, D1, D2, D3);  // AND_Gate
  and s15 (s15_out, D0, D1, D2, D3);
  or or_1 (or_1_out, s10_out, s0_out);
  or or_2 (or_2_out, s1_out, s11_out);
  or or_3 (or_3_out, s2_out, s12_out);
  or or_4 (or_4_out, s3_out, s13_out);
  or or_5 (or_5_out, s4_out, s14_out);
  or or_6 (or_6_out, s5_out, s15_out);
  or or_7 (or_7_out, s10_out, s11_out, s12_out, s13_out, s14_out, s15_out);
  not not_1 (B2, or_7_out);
  or or_8 (B1, or_1_out, or_3_out, or_6_out, or_4_out, s6_out, s8_out);
  or or_9 (BL1, or_1_out, or_3_out, s6_out, s8_out);
  or or_10 (BR1, or_1_out, or_2_out, or_4_out, or_5_out, or_6_out, s6_out, s7_out, s8_out, s9_out);
  or or_11 (M1, or_3_out, or_4_out, or_5_out, or_6_out, s6_out, s8_out, s9_out);
  or or_12 (TL1, or_1_out, or_5_out, or_6_out, s6_out, s8_out, s9_out);
  or or_13 (TR1, or_1_out, or_2_out, or_3_out, or_4_out, or_5_out, s7_out, s8_out, s9_out);
  or or_14 (T1, or_1_out, or_3_out, or_4_out, or_6_out, s6_out, s7_out, s8_out, s9_out);
  or or_15 (BR2, B2, or_7_out);
  or or_16 (TR2, B2, or_7_out);

  assign BL2 = B2;
  assign M2 = 1'b0;
  assign T2 = B2;
  assign TL2 = B2;
endmodule

module pcincr (
  input  in1,
  input  in2,
  input  in3,
  input  en,
  output out1,
  output out2,
  output out3
);

  wire and_1_out, and_2_out, and_4_out, and_5_out, and_7_out, and_8_out, and_10_out, not_1_out, not_2_out,
       not_3_out, or_1_out, or_2_out, or_3_out;

  and and_1 (and_1_out, and_2_out, and_4_out);
  and and_2 (and_2_out, in1, en);
  or or_1 (or_1_out, and_2_out, and_4_out);
  not not_1 (not_1_out, and_1_out);
  and and_3 (out1, not_1_out, or_1_out);
  and and_4 (and_4_out, and_5_out, and_7_out);
  not not_2 (not_2_out, and_4_out);
  and and_5 (and_5_out, in2, en);
  or or_2 (or_2_out, and_5_out, and_7_out);
  and and_6 (out2, not_2_out, or_2_out);
  and and_7 (and_7_out, and_8_out, and_10_out);
  and and_8 (and_8_out, in3, en);
  or or_3 (or_3_out, and_8_out, and_10_out);
  not not_3 (not_3_out, and_7_out);
  and and_9 (out3, not_3_out, or_3_out);
  and and_10 (and_10_out, 1'b1, en);
endmodule
